// Logisim project control-logic.circ as structural Verilog: 1 circuit, main circuit control_logic
module control_logic (
  input  [31:0] Instruction,
  input  BrEq,
  input  BrLt,
  output PCSel,
  output RegWEn,
  output [2:0] ImmSel,
  output BrUn,
  output ASel,
  output BSel,
  output [3:0] ALUSel,
  output MemWEn,
  output [1:0] WBSel
);

  wire and_1_out, and_2_out, and_3_out, comparator_1_eq, comparator_2_eq, comparator_3_eq, comparator_4_eq,
       comparator_5_eq, comparator_6_eq, comparator_7_eq, comparator_8_eq, comparator_9_eq, comparator_10_eq,
       comparator_11_eq, is_addi, is_andi, is_I_type, is_ori, is_slli, is_slti, is_srai, is_srli, is_xori;
  wire [5:0] ROMInput;
  wire [15:14] rom_1_data;

  ROM #(.addrWidth(6), .dataWidth(16)) rom_1 (
    .addr(ROMInput), .data({rom_1_data, WBSel, MemWEn, ALUSel, BSel, ASel, BrUn, ImmSel, RegWEn}));
  Priority_Encoder #(.select_enc(6)) priority_encoder_1 (
    .in15(is_addi), .in16(is_slli), .in17(is_slti), .in18(is_xori), .in19(is_srli), .in20(is_srai),
    .in21(is_ori), .in22(is_andi), .out(ROMInput));  // open: in0, in1, in2, in3, in4, in5, in6, in7, in8, in9, in10, in11, in12, in13, in14, in23, in24, in25, in26, in27, in28, in29, in30, in31, in32, in33, in34, in35, in36, in37, in38, in39, in40, in41, in42, in43, in44, in45, in46, in47, in48, in49, in50, in51, in52, in53, in54, in55, in56, in57, in58, in59, in60, in61, in62, in63, gs, en_out, en_in
  Comparator #(.width(3)) comparator_1 (.a(3'b001), .b(Instruction[14:12]), .eq(comparator_1_eq));  // open: gt, lt
  Comparator #(.width(3)) comparator_2 (.a(3'b101), .b(Instruction[14:12]), .eq(comparator_2_eq));  // open: gt, lt
  Comparator #(.width(3)) comparator_3 (.a(3'b101), .b(Instruction[14:12]), .eq(comparator_3_eq));  // open: gt, lt
  Comparator #(.width(7)) comparator_4 (.a({7{1'b0}}), .b(Instruction[31:25]), .eq(comparator_4_eq));  // open: gt, lt
  and and_1 (and_1_out, is_I_type, comparator_1_eq);
  Comparator #(.width(7)) comparator_5 (.a({7{1'b0}}), .b(Instruction[31:25]), .eq(comparator_5_eq));  // open: gt, lt
  and and_2 (and_2_out, is_I_type, comparator_2_eq);
  Comparator #(.width(7)) comparator_6 (.a(7'b0100000), .b(Instruction[31:25]), .eq(comparator_6_eq));  // open: gt, lt
  and and_3 (and_3_out, is_I_type, comparator_3_eq);
  Comparator #(.width(3)) comparator_7 (.a(3'b000), .b(Instruction[14:12]), .eq(comparator_7_eq));  // open: gt, lt
  and and_4 (is_slli, comparator_4_eq, and_1_out);
  Comparator #(.width(3)) comparator_8 (.a(3'b010), .b(Instruction[14:12]), .eq(comparator_8_eq));  // open: gt, lt
  Comparator #(.width(3)) comparator_9 (.a(3'b100), .b(Instruction[14:12]), .eq(comparator_9_eq));  // open: gt, lt
  and and_5 (is_srli, comparator_5_eq, and_2_out);
  and and_6 (is_srai, comparator_6_eq, and_3_out);
  Comparator #(.width(3)) comparator_10 (.a(3'b110), .b(Instruction[14:12]), .eq(comparator_10_eq));  // open: gt, lt
  Comparator #(.width(3)) comparator_11 (.a(3'b111), .b(Instruction[14:12]), .eq(comparator_11_eq));  // open: gt, lt
  Comparator #(.width(7)) comparator_12 (.a(7'b0010011), .b(Instruction[6:0]), .eq(is_I_type));  // open: gt, lt
  and and_7 (is_addi, is_I_type, comparator_7_eq);
  and and_8 (is_slti, is_I_type, comparator_8_eq);
  and and_9 (is_xori, is_I_type, comparator_9_eq);
  and and_10 (is_ori, is_I_type, comparator_10_eq);
  and and_11 (is_andi, is_I_type, comparator_11_eq);

  assign PCSel = 1'b0;

  // Notes on the sheet:
  //   INPUTS to your circuit
  //   contents of rom_1 (hex, n*v repeats v):
  //   15*0 1041 10c1 1141 1241 12c1 16c1 1341 13c1
  //   ROM FOR CONTROL LOGIC
  //   DON'T CHANGE THE LOCATIONS OF THE INPUTS AND OUTPUTS!
  //   This is only if you choose to do the ROM option
  //   OUTPUT from your circuit
endmodule
